# Fritzing sketch arm_pcb-3_5 (saved by Fritzing 0.9.3b)
circuit board: 10cm x 7.5cm

parts:
  A-Star_Mini = pololu-3104-astar-32u4-mini-sv-d [chip_label="Pololu A* 32U4 Mini SV"]
  Pololu_A1 = Pololu A4988 [package=SO16]
  Pololu_A2 = Pololu A4988 [package=SO16]
  Pololu_A3 = Pololu A4988 [package=SO16]
  Pololu_A6 = Pololu A4988 [package=SO16]
  Pololu_A5 = Pololu A4988 [package=SO16]
  Pololu_A4 = Pololu A4988 [package=SO16]
  0_1_2_3_4_5 = screw terminal, 6 pins
  J8 = screw terminal, 4 pins
  J7 = screw terminal, 4 pins
  J6 = screw terminal, 4 pins
  J12 = screw terminal, 4 pins
  J3 = screw terminal, 4 pins
  J4 = screw terminal, 4 pins
  C1 = Electrolytic Capacitor [capacitance=10μF package="100 mil [THT, electrolytic]"]
  C2 = Electrolytic Capacitor [capacitance=10μF package="100 mil [THT, electrolytic]"]
  C3 = Electrolytic Capacitor [capacitance=10μF package="100 mil [THT, electrolytic]"]
  C4 = Electrolytic Capacitor [capacitance=10μF package="100 mil [THT, electrolytic]"]
  C5 = Electrolytic Capacitor [capacitance=10μF package="100 mil [THT, electrolytic]"]
  C6 = Electrolytic Capacitor [capacitance=10μF package="100 mil [THT, electrolytic]"]
  J11 = Screw terminal - 2 pins [package=THT]
  C7 = Electrolytic Capacitor [capacitance=10μF package="100 mil [THT, electrolytic]"]
  C8 = Electrolytic Capacitor [capacitance=10μF package="100 mil [THT, electrolytic]"]
  C9 = Electrolytic Capacitor [capacitance=10μF package="100 mil [THT, electrolytic]"]
  C10 = Electrolytic Capacitor [capacitance=10μF package="100 mil [THT, electrolytic]"]
  C11 = Electrolytic Capacitor [capacitance=10μF package="100 mil [THT, electrolytic]"]
  C12 = Electrolytic Capacitor [capacitance=10μF package="100 mil [THT, electrolytic]"]
  Pow = screw terminal, 2 pins
  -_+ = Screw terminal - 2 pins [package=THT]
  J1 = Screw terminal - 2 pins [package=THT]
  J13 = screw terminal, 3 pins

nets:
  N1: A-Star_Mini.connector3, 0_1_2_3_4_5.pin1
  N2: A-Star_Mini.connector4, 0_1_2_3_4_5.pin2
  N3: A-Star_Mini.connector5, 0_1_2_3_4_5.pin3
  N4: A-Star_Mini.connector6, 0_1_2_3_4_5.pin4
  N5: A-Star_Mini.connector7, 0_1_2_3_4_5.pin5
  N6: A-Star_Mini.connector8, 0_1_2_3_4_5.pin6
  N7: A-Star_Mini.connector10, J13.pin1
  N8: A-Star_Mini.connector11, J13.pin2
  N9: A-Star_Mini.connector12, J1.pin1
  N10: A-Star_Mini.connector13, J13.pin3
  N11: A-Star_Mini.connector14, J1.pin2
  N12: A-Star_Mini.connector16, Pololu_A1.GND#8, Pololu_A2.GND, Pololu_A3.GND#8, Pololu_A6.GND#8, Pololu_A5.GND#8, Pololu_A4.GND#8, C7.-, C8.-, C9.-, C10.-, C11.-, C12.-, -_+.pin1
  VDD: A-Star_Mini.connector17, Pololu_A1.VDD, Pololu_A2.VDD, Pololu_A3.VDD, Pololu_A6.VDD, Pololu_A5.VDD, Pololu_A4.VDD, C7.+, C8.+, C9.+, C10.+, C11.+, C12.+, -_+.pin2
  N13: A-Star_Mini.connector18, J11.pin2
  N14: A-Star_Mini.connector19, J11.pin1
  N15: A-Star_Mini.connector20, Pololu_A1.ENABLE, Pololu_A2.ENABLE, Pololu_A3.ENABLE, Pololu_A6.ENABLE, Pololu_A5.ENABLE, Pololu_A4.ENABLE
  N16: A-Star_Mini.connector21, Pololu_A1.DIR
  N17: A-Star_Mini.connector22, Pololu_A1.STEP
  N18: A-Star_Mini.connector23, Pololu_A2.DIR
  N19: A-Star_Mini.connector24, Pololu_A2.STEP
  N20: A-Star_Mini.connector25, Pololu_A3.DIR
  N21: A-Star_Mini.connector26, Pololu_A3.STEP
  N22: A-Star_Mini.connector27, Pololu_A4.DIR
  N23: A-Star_Mini.connector28, Pololu_A4.STEP
  N24: A-Star_Mini.connector29, Pololu_A5.DIR
  N25: A-Star_Mini.connector30, Pololu_A5.STEP
  N26: A-Star_Mini.connector31, Pololu_A6.DIR
  N27: A-Star_Mini.connector32, Pololu_A6.STEP
  N28: A-Star_Mini.connector34, A-Star_Mini.connector36, A-Star_Mini.connector37, A-Star_Mini.connector38, A-Star_Mini.connector39
  N29: Pololu_A1.RESET, Pololu_A1.SLEEP
  N30: Pololu_A1.1B, J6.pin4
  N31: Pololu_A1.1A, J6.pin3
  N32: Pololu_A1.2A, J6.pin2
  N33: Pololu_A1.2B, J6.pin1
  N34: Pololu_A1.GND#14, Pololu_A3.GND#14, Pololu_A6.GND#14, Pololu_A5.GND#14, Pololu_A4.GND#14, C1.-, C2.-, C3.-, C4.-, C5.-, C6.-, Pow.pin2
  N35: Pololu_A1.VMOT, Pololu_A2.VMOT, Pololu_A3.VMOT, Pololu_A6.VMOT, Pololu_A5.VMOT, Pololu_A4.VMOT, C1.+, C2.+, C3.+, C4.+, C5.+, C6.+, Pow.pin1
  N36: Pololu_A2.RESET, Pololu_A2.SLEEP
  N37: Pololu_A2.1B, J7.pin4
  N38: Pololu_A2.1A, J7.pin3
  N39: Pololu_A2.2A, J7.pin2
  N40: Pololu_A2.2B, J7.pin1
  N41: Pololu_A3.RESET, Pololu_A3.SLEEP
  N42: Pololu_A3.1B, J8.pin4
  N43: Pololu_A3.1A, J8.pin3
  N44: Pololu_A3.2A, J8.pin2
  N45: Pololu_A3.2B, J8.pin1
  N46: Pololu_A6.RESET, Pololu_A6.SLEEP
  N47: Pololu_A6.1B, J4.pin4
  N48: Pololu_A6.1A, J4.pin3
  N49: Pololu_A6.2A, J4.pin2
  N50: Pololu_A6.2B, J4.pin1
  N51: Pololu_A5.RESET, Pololu_A5.SLEEP
  N52: Pololu_A5.1B, J3.pin4
  N53: Pololu_A5.1A, J3.pin3
  N54: Pololu_A5.2A, J3.pin2
  N55: Pololu_A5.2B, J3.pin1
  N56: Pololu_A4.RESET, Pololu_A4.SLEEP
  N57: Pololu_A4.1B, J12.pin4
  N58: Pololu_A4.1A, J12.pin3
  N59: Pololu_A4.2A, J12.pin2
  N60: Pololu_A4.2B, J12.pin1

notes:
  Jenny 5 arm electronics
  jenny5.org
